# Fritzing sketch LoRa_PlantGuard (saved by Fritzing 0.9.4)
circuit board: 6.37847cm x 4.8038cm
breadboards: 1

parts:
  Q1 = Arduino Pro Mini v13
  RFM95W_1 = female pin header, 8 pins [form="♀ (female)"]
  RFM95W_2 = female pin header, 8 pins [form="♀ (female)"]
  Sensor3 = female pin header, 3 pins [form="♀ (female)"]
  Sensor2 = female pin header, 3 pins [form="♀ (female)"]
  Sensor1 = female pin header, 3 pins [form="♀ (female)"]
  Sensor0 = female pin header, 3 pins [form="♀ (female)"]
  ADS1115_2 = female pin header, 4 pins [form="♀ (female)"]
  ADS1115_1 = female pin header, 4 pins [form="♀ (female)"]
  BME280 = female pin header, 4 pins [form="♀ (female)"]
  IRLML6402 = female pin header, 3 pins [form="♀ (female)"]
  Buck_3v3 = female pin header, 4 pins [form="♀ (female)"]
  I2C = female pin header, 2 pins [form="♀ (female)"]
  C1 = Electrolytic Capacitor [capacitance=1µF package="200 mil [THT, electrolytic]"]
  VCC1 = Battery
  ICSP2 = female pin header, 3 pins [form="♀ (female)"]
  ICSP3 = female pin header, 3 pins [form="♀ (female)"]

nets:
  N1: Q1.VCC, RFM95W_2.pin5, IRLML6402.pin3, C1.+, VCC1.+, ICSP2.pin3
  N2: Q1.A4, ADS1115_1.pin4, BME280.pin4, I2C.pin2
  N3: Q1.A5, ADS1115_1.pin3, BME280.pin3, I2C.pin1
  N4: Q1.GND, RFM95W_1.pin1, RFM95W_1.pin8, RFM95W_2.pin2, Sensor3.pin3, Sensor2.pin3, Sensor1.pin3, Sensor0.pin3, ADS1115_1.pin2, BME280.pin2, Buck_3v3.pin2, C1.-, VCC1.-, ICSP2.pin1
  N5: Q1.RESET, ICSP2.pin2
  N6: Q1.D13/SCK, RFM95W_1.pin5, ICSP3.pin1
  N7: Q1.D12/MISO, RFM95W_1.pin7, ICSP3.pin2
  N8: Q1.D11_PWM/MOSI, RFM95W_1.pin6, ICSP3.pin3
  N9: Q1.D10_PWM/SS, RFM95W_1.pin4
  N10: Q1.D9_PWM, RFM95W_1.pin3
  N11: Q1.D5_PWM, IRLML6402.pin1
  N12: Q1.D3_PWM, RFM95W_2.pin7
  N13: Q1.D2, RFM95W_2.pin6
  N14: Sensor3.pin1, ADS1115_2.pin4
  N15: Sensor3.pin2, Sensor2.pin2, Sensor1.pin2, Sensor0.pin2, ADS1115_1.pin1, BME280.pin1, Buck_3v3.pin1
  N16: Sensor2.pin1, ADS1115_2.pin3
  N17: Sensor1.pin1, ADS1115_2.pin2
  N18: Sensor0.pin1, ADS1115_2.pin1
  N19: IRLML6402.pin2, Buck_3v3.pin3
